// Logisim project cpu.circ as structural Verilog: 1 circuit, main circuit main
module main (
  input  [31:0] INSTRUCTION,
  input  CLOCK,
  output [31:0] PROGRAM_COUNTER,
  output [31:0] ra,
  output [31:0] sp,
  output [31:0] t0,
  output [31:0] t1,
  output [31:0] t2,
  output [31:0] s0,
  output [31:0] s1,
  output [31:0] a0
);

  wire control_logic_1_memrw, RegWEn;
  wire [1:0] control_logic_1_wbsel;
  wire [2:0] control_logic_1_immsel;
  wire [3:0] control_logic_1_alusel;
  wire [4:0] rd, rs1, rs2;
  wire [31:0] ALURes, DMEM_p3, imm, pc, RegFile_read_data_1, register_1_q, wb;

  control_logic control_logic_1 (
    .ImmSel(control_logic_1_immsel), .RegWEn(RegWEn),
    .inst({register_1_q[31:25], rs2, rs1, register_1_q[14:12], rd, register_1_q[6:0]}),
    .ALUSel(control_logic_1_alusel), .MemRW(control_logic_1_memrw), .WBSel(control_logic_1_wbsel));  // open: BSel, ASel, BrUn, PCSel, BrLt, BrEq
  Register #(.width(32)) register_1 (
    .D(INSTRUCTION), .clk(CLOCK),
    .Q({register_1_q[31:25], rs2, rs1, register_1_q[14:12], rd, register_1_q[6:0]}));  // open: en, clr
  Adder #(.width(32)) adder_1 (.a(PROGRAM_COUNTER), .b(32'h4), .out(pc));  // open: cin, cout
  Register #(.width(32)) u_PC (.D(pc), .clk(CLOCK), .Q(PROGRAM_COUNTER));  // open: en, clr
  imm_gen imm_gen_1 (
    .ImmSel(control_logic_1_immsel),
    .inst({register_1_q[31:25], rs2, rs1, register_1_q[14:12], rd, register_1_q[6:0]}), .imm(imm));
  // branch_comp branch_comp_1: pin names not known
  regfile_main RegFile (
    .rs2(rs2), .rd(rd), .Read_Data_1(RegFile_read_data_1), .ra(ra), .sp(sp), .t0(t0), .t1(t1), .t2(t2),
    .s0(s0), .s1(s1), .a0(a0), .rs1(rs1), .Write_Data(wb), .RegWEn(RegWEn), .clk(CLOCK));  // open: Read_Data_2
  alu Arithmetic_Logic_Unit (.Result(ALURes), .ALUSel(control_logic_1_alusel), .A(RegFile_read_data_1), .B(imm));
  // mem_main DMEM: pin names not known; wires that end beside it: CLOCK, control_logic_1_memrw, DMEM_p3
  Multiplexer #(.select(2), .width(32), .enable("false")) multiplexer_1 (
    .in1(ALURes), .in2(DMEM_p3), .in3(pc), .out(wb), .sel(control_logic_1_wbsel));  // open: in0

  // Other names for the same wires on the sheet: clk = CLOCK

  // Notes on the sheet:
  //   Output
  //   IMEM (do **NOT** move this)
  //   Inputs
  //   It is OK to move the PC, RegFile, ALU, MEM, Branch Comp, Imm Gen, and Control Logic to wherever is most convenient for you when constructing your CPU, and to delete this text
  //   Inputs/Outputs for testing. Do **NOT** move these.
endmodule
